# Fritzing sketch Buzzer_Buttons (saved by Fritzing 0.9.4)
breadboards: 1

parts:
  Part1 = Arduino Uno (Rev3) - ICSP
  J1 = Piezo Speaker
  S1 = Pushbutton [package="[SMD]"]
  S2 = Pushbutton [package="[SMD]"]
  R1 = Resistor [tolerance=±5% resistance=10k package="0402 [SMD]"]
  R2 = Resistor [tolerance=±5% resistance=10k package="0402 [SMD]"]

nets:
  N1: Part1.D9_PWM, J1.pin2
  N2: Part1.D5_PWM, S2.Pin_3, S2.Pin_4, R2.Pin_0
  N3: Part1.D6_PWM, S1.Pin_3, S1.Pin_4, R1.Pin_0
  N4: S1.Pin_1, S1.Pin_2, S2.Pin_1, S2.Pin_2
  N5: R1.Pin_1, R2.Pin_1
