# Fritzing sketch Mic_RGBLED (saved by Fritzing 0.9.4)
breadboards: 1

parts:
  Part1 = Arduino Uno (Rev3)
  LED1 = RGB LED (com. anode, rbg) [package="5 mm [THT]"]
  R1 = Resistor [tolerance=±5% resistance=220 package="0805 [SMD]"]
  R2 = Resistor [tolerance=±5% resistance=220 package="0805 [SMD]"]
  R3 = Resistor [tolerance=±5% resistance=220 package="0805 [SMD]"]
  Part2 = KY-037 High Sensitivity Sound Detection Module [package="Breakout board"]

nets:
  N1: Part1.A0, Part2.A0
  N2: Part1.D10_PWM/SS, R3.Pin_1
  N3: Part1.D11_PWM/MOSI, R2.Pin_1
  N4: Part1.D12/MISO, R1.Pin_1
  N5: Part1.GND, LED1.common_anode, Part2.G
  N6: Part1.5V, Part2.+
  N7: LED1.red_cathode, R1.Pin_0
  N8: LED1.blue_cathode, R2.Pin_0
  N9: LED1.green_cathode, R3.Pin_0

custom parts:
  KY-037 High Sensitivity Sound Detection Module: KY-037 high sensitivity sound detection module is an analog/digital sensor that uses a condenser microphone to observe changes in environment noise.
