# Fritzing sketch Number Display (saved by Fritzing 0.9.4)
breadboards: 1

parts:
  Part1 = Arduino Uno (Rev3)
  R1 = Resistor [tolerance=±5% resistance=220 package="2512 [SMD]"]
  R2 = Resistor [tolerance=±5% resistance=220 package="0402 [SMD]"]
  R3 = Resistor [tolerance=±5% resistance=220 package="1206 [SMD]"]
  7_Segment_4_Digit_Display1 = 7-SEGMENT-4DIGIT common cathode [part_number=HS420561K-32 package=7-segment-4digit-cathode]
  R4 = Resistor [tolerance=±5% resistance=220 package="1206 [SMD]"]

nets:
  N1: Part1.D8, 7_Segment_4_Digit_Display1.pin_4
  N2: Part1.D9_PWM, 7_Segment_4_Digit_Display1.pin_2
  N3: Part1.D10_PWM/SS, 7_Segment_4_Digit_Display1.pin_1
  N4: Part1.D11_PWM/MOSI, 7_Segment_4_Digit_Display1.pin_10
  N5: Part1.D12/MISO, 7_Segment_4_Digit_Display1.pin_5
  N6: Part1.D13/SCK, 7_Segment_4_Digit_Display1.pin_3
  N7: Part1.D2, R1.Pin_0
  N8: Part1.D3_PWM, R2.Pin_0
  N9: Part1.D4, R3.Pin_0
  N10: Part1.D6_PWM, 7_Segment_4_Digit_Display1.pin_11
  N11: Part1.D7, 7_Segment_4_Digit_Display1.pin_7
  N12: 7_Segment_4_Digit_Display1.pin_6, R4.Pin_0

custom parts:
  7-SEGMENT-4DIGIT common cathode: A 7 Segment 4 Digit common cathode display, with decimal points
