# Fritzing sketch Project (saved by Fritzing 0.9.4)
breadboards: 1

parts:
  Part1 = Arduino Uno (Rev3)
  Part2 = Arduino Uno (Rev3)
  Part3 = Arduino Uno (Rev3)
  Part4 = Arduino Uno (Rev3)
  U1 = LCD-16X2 [package=lcd-16x2_noholes]
  Mod1 = KY-022 Infrared Receiver Module [package="Breakout board"]
  Part5 = KY-037 High Sensitivity Sound Detection Module [package="Breakout board"]
  RGB_Strip_LED1 = RGB Strip LED
  U2 = 74HC595 [package="DIP16 [THT]"]
  7_Segment_4_Digit_Display3 = 7-SEGMENT-4DIGIT common cathode [part_number=HS420561K-32 package=7-segment-4digit-cathode]
  R1 = Resistor [tolerance=±5% resistance=220 package=THT]
  R2 = Resistor [tolerance=±5% resistance=220 package=THT]
  R3 = Resistor [tolerance=±5% resistance=220 package=THT]
  R4 = Resistor [tolerance=±5% resistance=220 package=THT]
  S1 = Pushbutton [package="[THT]"]
  S2 = Pushbutton [package="[THT]"]
  R5 = Resistor [tolerance=±5% resistance=10k package="1206 [SMD]"]
  R6 = Resistor [tolerance=±5% resistance=10k package="1206 [SMD]"]

nets:
  N1: Part1.A0, Part5.A0
  N2: Part1.A4/SDA, Part2.A4/SDA, Part3.A4/SDA, Part4.A4/SDA
  N3: Part1.A5/SCL, Part2.A5/SCL, Part3.A5/SCL, Part4.A5/SCL
  GND: Part1.GND, Part2.GND, Part3.GND, Part4.GND, U1.VSS, U1.VO, U1.R_W, U1.K, Mod1.-, Part5.G, U2.GND, U2.OE, 7_Segment_4_Digit_Display3.pin_8, R1.Pin_0, R2.Pin_0, R2.Pin_1, R3.Pin_0, R4.Pin_0, R5.Pin_0, R6.Pin_0
  5V: Part1.5V, Part2.5V, Part3.5V, Part4.5V, U1.VDD, U1.A, Mod1.Vin, Part5.+, RGB_Strip_LED1.Common_Connect, U2.VCC, S1.Pin_3, S1.Pin_4, S2.Pin_3, S2.Pin_4
  N4: Part2.D8, U2.DS
  N5: Part2.D9_PWM, U2.ST_CP
  N6: Part2.D10_PWM/SS, U2.SH_CP
  N7: Part3.D8, S2.Pin_1, S2.Pin_2, R6.Pin_1
  N8: Part3.D9_PWM, S1.Pin_1, S1.Pin_2, R5.Pin_1
  N9: Part3.D10_PWM/SS, RGB_Strip_LED1.Green_Connect
  N10: Part3.D11_PWM/MOSI, RGB_Strip_LED1.Red_Connect
  N11: Part3.D12/MISO, RGB_Strip_LED1.Blue_Connect
  N12: Part4.D8, U1.E
  N13: Part4.D9_PWM, U1.DB4
  N14: Part4.D10_PWM/SS, U1.DB5
  N15: Part4.D11_PWM/MOSI, U1.DB6
  N16: Part4.D12/MISO, U1.DB7
  N17: Part4.D6_PWM, Mod1.S
  N18: Part4.D7, U1.RS
  N19: U2.Q1, 7_Segment_4_Digit_Display3.pin_7
  N20: U2.Q2, 7_Segment_4_Digit_Display3.pin_4
  N21: U2.Q3, 7_Segment_4_Digit_Display3.pin_2
  N22: U2.Q4, 7_Segment_4_Digit_Display3.pin_1
  N23: U2.Q5, 7_Segment_4_Digit_Display3.pin_10
  N24: U2.Q6, 7_Segment_4_Digit_Display3.pin_5
  N25: U2.Q7, 7_Segment_4_Digit_Display3.pin_3
  N26: U2.Q0, 7_Segment_4_Digit_Display3.pin_11
  N27: 7_Segment_4_Digit_Display3.pin_6, R1.Pin_1
  N28: 7_Segment_4_Digit_Display3.pin_9, R3.Pin_1
  N29: 7_Segment_4_Digit_Display3.pin_12, R4.Pin_1

custom parts:
  KY-022 Infrared Receiver Module: KY-022 IR receiver module, reacts to 38kHz infrared light.
  KY-037 High Sensitivity Sound Detection Module: KY-037 high sensitivity sound detection module is an analog/digital sensor that uses a condenser microphone to observe changes in environment noise.
  RGB Strip LED: A tri-color Strip LED with red, green and blue. Based on LED SMD 5050 RGB Pin order: common cathode - green - red - blue
  7-SEGMENT-4DIGIT common cathode: A 7 Segment 4 Digit common cathode display, with decimal points
